# Fritzing sketch diagram_pas_throttle (saved by Fritzing 0.9.10b)
circuit board: 8.46667cm x 5.64444cm
perfboards: 1

parts:
  R1 = Resistor [tolerance=±1% power=0.25 resistance=1k package=THT]
  J3 = female pin header, 3 pins [form="♀ (female)"]
  J4 = female pin header, 3 pins [form="♀ (female)"]
  Composant1 = Arduino Nano (Rev3.0)
  C1 = Electrolytic Capacitor [capacitance=0.1µF voltage=35V package="100 mil [THT, electrolytic]"]

nets:
  N1: R1.Pin_0, Composant1.D10
  N2: R1.Pin_1, J3.pin3, C1.+
  N3: J3.pin2, J4.pin2, Composant1.GND, C1.-
  N4: J4.pin1, Composant1.D2
  N5: J4.pin3, Composant1.5V

notes:
  Controler (throttle)
  + Vin (7V-12V)
  Common GND
  +5V arduino
  Signal (PWM D10)
  Gnd
  Signal (D2)
  e-bike PAS
  LED BUILTIN (D13)
  +
  +5V
  S
  RC filter
  not mandatory, to be tested
  (with controler)
  PAS to throttle, Chris74
